# Fritzing sketch Pong-2-Player-Gyro (saved by Fritzing 1.0.2b)
breadboards: 1

parts:
  Bauteil1 = Arduino Nano (Rev3.0)
  GY1 = MPU-6050 Board GY-521 [form="♀ (female)" package=THT]
  GY2 = MPU-6050 Board GY-521 [form="♀ (female)" package=THT]
  TFT1 = 1.44" SPI TFT Graphics Display 128x128 [package=THT]
  S1 = Pushbutton [package="[THT]"]
  S2 = Pushbutton [package="[THT]"]

nets:
  N1: Bauteil1.GND, GY1.pin2, GY2.pin2, TFT1.pin1, S1.Pin_3, S1.Pin_4, S2.Pin_3, S2.Pin_4
  N2: Bauteil1.D2, S1.Pin_1, S1.Pin_2
  N3: Bauteil1.D3, S2.Pin_1, S2.Pin_2
  N4: Bauteil1.D8, TFT1.pin5
  N5: Bauteil1.D9, TFT1.pin6
  N6: Bauteil1.D10, TFT1.pin7
  N7: Bauteil1.D11/MOSI, TFT1.pin4
  N8: Bauteil1.5V, GY1.pin1, GY2.pin1, GY2.pin7, TFT1.pin2
  N9: Bauteil1.A5, GY1.pin3, GY2.pin3
  N10: Bauteil1.A4, GY1.pin4, GY2.pin4
  N11: Bauteil1.D13/SCK, TFT1.pin3

custom parts:
  MPU-6050 Board GY-521: Acelerometro y Giroscopio MPU-6050 Board GY-521
